// Logisim project L8.circ as structural Verilog: 5 circuits, main circuit main
module main (
  input  in_1,
  input  in_2,
  input  in_3
);

  wire clk2_1_c, clock_1_out, ctrl_1_cn, ctrl_1_m, ctrl_1_sel_ip, ctrl_1_yrw, nand_1_out, not_1_out,
       not_2_out, not_3_out, not_4_out, not_5_out;
  wire [1:0] ctrl_1_muxa, multiplexer_1_out, multiplexer_2_out;
  wire [2:0] ctrl_1_state;
  wire [3:0] ctrl_1_fn_sel, IR_q, IR_q_2;
  wire [4:0] ctrl_1_mar;
  wire [7:0] ALU_f, MAR_q, MBR_q, multiplexer_3_out, ram_1_data, reg_1_qa, reg_1_qb, register_1_q;
  wire [31:0] reg_1_test;

  clk2 clk2_1 (.halt(in_1), .step(in_2), .clock(clock_1_out), .rest(in_3), .C(clk2_1_c));
  Clock clock_1 (.out(clock_1_out));
  Register MAR (.D(reg_1_qa), .Q(MAR_q), .clk(register_1_q[0]));  // open: en, clr
  // Probe on ctrl_1_state
  ctrl ctrl_1 (
    .clock(clk2_1_c), .IR(IR_q), .y(IR_q_2[1:0]), .state(ctrl_1_state), .MAR(ctrl_1_mar[0]),
    .SEL_IP(ctrl_1_sel_ip), .IR_2(ctrl_1_mar[2]), .MBR(ctrl_1_mar[1]), .WR(ctrl_1_mar[3]),
    .WM(ctrl_1_mar[4]), .MUXa(ctrl_1_muxa[0]), .MUXb(ctrl_1_muxa[1]), .YRW(ctrl_1_yrw),
    .FN_SEL(ctrl_1_fn_sel), .m(ctrl_1_m), .cn(ctrl_1_cn));  // open: zero, z, cf
  not not_1 (not_1_out, register_1_q[4]);
  // Probe on ram_1_data
  RAM #(.bus("asynch")) ram_1 (.addr(MAR_q), .data(ram_1_data), .ld(not_1_out));  // open: sel, clr
  not not_2 (not_2_out, register_1_q[4]);
  Register IR (.D(ram_1_data), .Q({IR_q, IR_q_2}), .clk(register_1_q[2]));  // open: en, clr
  Register register_1 (.D({3'b111, ctrl_1_mar}), .Q(register_1_q), .clk(clk2_1_c), .clr(not_3_out));  // open: en
  not not_3 (not_3_out, nand_1_out);
  // Probe on IR_q_2[1:0]
  Multiplexer #(.width(2), .enable("false")) multiplexer_1 (
    .in0(multiplexer_2_out), .in1(IR_q_2[1:0]), .out(multiplexer_1_out), .sel(ctrl_1_yrw));
  Multiplexer #(.width(2), .enable("false")) multiplexer_2 (
    .in0(2'b11), .in1(IR_q_2[3:2]), .out(multiplexer_2_out), .sel(ctrl_1_sel_ip));
  nand nand_1 (nand_1_out, ~clk2_1_c, register_1_q[7]);  // NAND_Gate
  // Probe on multiplexer_2_out
  not not_4 (not_4_out, register_1_q[3]);
  Register MBR (.D(ALU_f), .Q(MBR_q), .clk(register_1_q[1]));  // open: en, clr
  \reg  reg_1 (
    .GrA(1'b0), .RA(multiplexer_2_out), .D(MBR_q), .Gw(not_4_out), .wa(multiplexer_1_out), .GrB(1'b0),
    .RB(IR_q_2[1:0]), .Qa(reg_1_qa), .Qb(reg_1_qb), .test(reg_1_test));
  // Probe on reg_1_test
  assign ram_1_data = not_5_out ? MBR_q : 8'bz;  // Controlled_Buffer controlled_buffer_1
  not not_5 (not_5_out, not_2_out);
  Multiplexer #(.select(2), .width(8), .enable("false")) multiplexer_3 (
    .in0(reg_1_qa), .in1(ram_1_data), .in2(reg_1_qb), .in3(reg_1_qb), .out(multiplexer_3_out),
    .sel(ctrl_1_muxa));
  alu ALU (
    .X(multiplexer_3_out), .Y(reg_1_qb), .M(ctrl_1_m), .Cn(ctrl_1_cn), .S(ctrl_1_fn_sel), .F(ALU_f));  // open: Cn_4, A_B
  // Probe on ram_1_data
  // Probe on multiplexer_3_out
  // Probe on reg_1_qb
  // Probe on ALU_f
endmodule

module ctrl (
  input  clock,
  input  [3:0] IR,
  input  [1:0] y,
  input  zero,
  output MAR,
  output [2:0] state,
  output SEL_IP,
  output IR_2,
  output MBR,
  output WR,
  output WM,
  output MUXa,
  output MUXb,
  output YRW,
  output [3:0] FN_SEL,
  output m,
  output cn,
  output z,
  output cf
);

  wire ADC, ADD, AND, and_1_out, and_2_out, and_3_out, DEC, INC, LD, multiplexer_1_out, n74154_1_y10,
       n74154_1_y11, n74154_1_y12, n74154_1_y13, NOT, not_1_out, not_2_out, OR, or_1_out, SBC, STR, SUB, T0,
       T1, T2, T3, T6, T7, XOR;

  _74154 u_74154_1 (
    .iE0(1'b0), .iE1(1'b0), .A0(IR[0]), .A1(IR[1]), .A2(IR[2]), .A3(IR[3]), .Y0(DEC), .Y1(ADD), .Y2(ADC),
    .Y3(SUB), .Y4(SBC), .Y5(AND), .Y6(OR), .Y7(XOR), .Y8(NOT), .Y9(INC), .Y10(n74154_1_y10),
    .Y11(n74154_1_y11), .Y12(n74154_1_y12), .Y13(n74154_1_y13), .Y14(LD), .Y15(STR));
  not not_1 (not_1_out, clock);
  Multiplexer #(.select(3), .disabled(0), .enable("false")) multiplexer_1 (
    .in0(1'b1), .in1(1'b1), .in2(1'b1), .in3(1'b0), .in4(1'b1), .in5(1'b1), .in6(1'b1), .in7(1'b1),
    .out(multiplexer_1_out), .sel({T1, STR, LD}));
  _74163 u_74163_1 (
    .D0(1'b0), .D1(1'b0), .D2(1'b1), .D3(1'b0), .CET(1'b1), .CEP(1'b1), .PE(multiplexer_1_out), .MR(T7),
    .CP(not_1_out), .Q0(state[0]), .Q1(state[1]), .Q2(state[2]));  // open: Q3, TC
  _74138 u_74138_1 (
    .E3(1'b1), .iE2(1'b0), .iE1(1'b0), .A0(state[0]), .A1(state[1]), .A2(state[2]), .Y0(T0), .Y1(T1),
    .Y2(T2), .Y3(T3), .Y4(T6), .Y5(T7));  // open: Y6, Y7
  Multiplexer #(.select(3), .disabled(0)) multiplexer_2 (
    .in0(1'b1), .in1(1'b1), .in2(1'b1), .in3(1'b0), .in4(1'b0), .in5(1'b1), .in6(1'b0), .in7(1'b0),
    .out(FN_SEL[3]), .sel(IR[2:0]), .en(not_2_out));
  Multiplexer #(.select(3), .disabled(0)) multiplexer_3 (
    .in0(1'b1), .in1(1'b0), .in2(1'b0), .in3(1'b1), .in4(1'b1), .in5(1'b1), .in6(1'b1), .in7(1'b1),
    .out(FN_SEL[2]), .sel(IR[2:0]), .en(not_2_out));
  Multiplexer #(.select(3), .disabled(0)) multiplexer_4 (
    .in0(1'b1), .in1(1'b0), .in2(1'b0), .in3(1'b1), .in4(1'b1), .in5(1'b0), .in6(1'b1), .in7(1'b1),
    .out(FN_SEL[1]), .sel(IR[2:0]), .en(not_2_out));
  Multiplexer #(.select(3), .disabled(0)) multiplexer_5 (
    .in0(1'b1), .in1(1'b1), .in2(1'b1), .in3(1'b0), .in4(1'b0), .in5(1'b1), .in6(1'b1), .in7(1'b0),
    .out(FN_SEL[0]), .sel(IR[2:0]), .en(not_2_out));
  not not_2 (not_2_out, or_1_out);
  or or_1 (or_1_out, IR[3], T6);
  and and_1 (and_1_out, AND, OR, XOR, NOT);
  and and_2 (and_2_out, ADC, SUB, INC);
  and and_3 (and_3_out, XOR, SUB, INC, ADD);
  nand nand_1 (MAR, T0, T2);
  and and_4 (SEL_IP, T0, T1);
  not not_3 (IR_2, T1);
  nand nand_2 (MBR, T0, T2, T6);
  Multiplexer #(.select(3), .enable("false")) multiplexer_6 (
    .in0(1'b0), .in2(1'b0), .in3(STR), .in4(1'b0), .in5(1'b1), .in6(1'b1), .in7(1'b0), .out(WR),
    .sel({T7, T3, T1}));  // open: in1
  nor nor_1 (WM, STR, T7);
  nor nor_2 (MUXa, LD, T6);
  nor nor_3 (MUXb, STR, T6);
  nor nor_4 (YRW, T7, LD);
  nor nor_5 (m, and_1_out, T6);
  and and_5 (cn, and_2_out, ~T6);  // AND_Gate
  nor nor_6 (z, and_3_out, T6);

  assign cf = 1'b0;
endmodule

module alu (
  input  [7:0] X,
  input  [7:0] Y,
  input  M,
  input  Cn,
  input  [3:0] S,
  output Cn_4,
  output A_B,
  output [7:0] F
);

  wire n74181_1_a_b, n74181_1_cn_4, n74181_2_a_b;

  _74181 u_74181_1 (
    .S3(S[3]), .S2(S[2]), .S1(S[1]), .S0(S[0]), .B3(Y[3]), .A3(X[3]), .B2(Y[2]), .A2(X[2]), .B1(Y[1]),
    .A1(X[1]), .B0(Y[0]), .A0(X[0]), .M(M), .Cn(Cn), .Cn_4(n74181_1_cn_4), .F3(F[3]), .F2(F[2]),
    .A_B(n74181_1_a_b), .F1(F[1]), .F0(F[0]));  // open: G, P
  _74181 u_74181_2 (
    .S3(S[3]), .S2(S[2]), .S1(S[1]), .S0(S[0]), .B3(Y[7]), .A3(X[7]), .B2(Y[6]), .A2(X[6]), .B1(Y[5]),
    .A1(X[5]), .B0(Y[4]), .A0(X[4]), .M(M), .Cn(n74181_1_cn_4), .Cn_4(Cn_4), .F3(F[7]), .F2(F[6]),
    .A_B(n74181_2_a_b), .F1(F[5]), .F0(F[4]));  // open: G, P
  and and_1 (A_B, n74181_1_a_b, n74181_2_a_b);

  // Other names for the same wires on the sheet: XL[3:0] = X[3:0]; XH[3:0] = X[7:4]; YL[3:0] = Y[3:0];
  //   YH[3:0] = Y[7:4]
endmodule

module \reg  (
  input  GrA,
  input  [1:0] RA,
  input  [7:0] D,
  input  Gw,
  input  [1:0] wa,
  input  GrB,
  input  [1:0] RB,
  output [7:0] Qa,
  output [7:0] Qb,
  output [31:0] test
);

  wire decoder_1_out0, decoder_1_out1, decoder_1_out2, decoder_1_out3, decoder_2_out0, decoder_2_out1,
       decoder_2_out2, decoder_2_out3, not_1_out, not_2_out, not_3_out, not_4_out;
  wire [7:0] register_1_q, register_3_q, register_5_q, register_7_q;

  not not_1 (not_1_out, Gw);
  Decoder #(.select(2), .disabled(0), .enable("false")) decoder_1 (
    .out0(decoder_1_out0), .out1(decoder_1_out1), .out2(decoder_1_out2), .out3(decoder_1_out3), .sel(wa));
  not not_2 (not_2_out, Gw);
  Decoder #(.select(2), .disabled(0), .enable("false")) decoder_2 (
    .out0(decoder_2_out0), .out1(decoder_2_out1), .out2(decoder_2_out2), .out3(decoder_2_out3), .sel(wa));
  Register #(.trigger("high")) register_1 (.D(D), .en(not_1_out), .Q(register_1_q), .clk(decoder_1_out0));  // open: clr
  Register #(.trigger("high")) register_2 (.D(D), .en(not_2_out), .Q(test[7:0]), .clk(decoder_2_out0));  // open: clr
  Register #(.trigger("high")) register_3 (.D(D), .en(not_1_out), .Q(register_3_q), .clk(decoder_1_out1));  // open: clr
  Register #(.trigger("high")) register_4 (.D(D), .en(not_2_out), .Q(test[15:8]), .clk(decoder_2_out1));  // open: clr
  Register #(.trigger("high")) register_5 (.D(D), .en(not_1_out), .Q(register_5_q), .clk(decoder_1_out2));  // open: clr
  Register #(.trigger("high")) register_6 (.D(D), .en(not_2_out), .Q(test[23:16]), .clk(decoder_2_out2));  // open: clr
  not not_3 (not_3_out, GrA);
  Multiplexer #(.select(2), .width(8)) multiplexer_1 (
    .in0(register_1_q), .in1(register_3_q), .in2(register_5_q), .in3(register_7_q), .out(Qa), .sel(RA),
    .en(not_3_out));
  Register #(.trigger("high")) register_7 (.D(D), .en(not_1_out), .Q(register_7_q), .clk(decoder_1_out3));  // open: clr
  not not_4 (not_4_out, GrB);
  Multiplexer #(.select(2), .width(8)) multiplexer_2 (
    .in0(test[7:0]), .in1(test[15:8]), .in2(test[23:16]), .in3(test[31:24]), .out(Qb), .sel(RB),
    .en(not_4_out));
  Register #(.trigger("high")) register_8 (.D(D), .en(not_2_out), .Q(test[31:24]), .clk(decoder_2_out3));  // open: clr
endmodule

module clk2 (
  input  halt,
  input  step,
  input  clock,
  input  rest,
  output C
);

  wire and_1_out, and_2_out, and_3_out, and_4_out, d_ff_1_q, d_ff_1_qn, d_ff_2_q, d_ff_2_qn, not_1_out,
       not_2_out;

  and and_1 (and_1_out, ~halt, d_ff_2_qn);  // AND_Gate
  and and_2 (and_2_out, d_ff_1_qn, halt);
  not not_1 (not_1_out, step);
  not not_2 (not_2_out, clock);
  D_Flip_Flop d_ff_1 (.clk(not_1_out), .D(and_1_out), .Q(d_ff_1_q), .Qn(d_ff_1_qn), .reset(rest));  // open: preset, en
  D_Flip_Flop d_ff_2 (.clk(not_2_out), .D(and_2_out), .Q(d_ff_2_q), .Qn(d_ff_2_qn), .reset(rest));  // open: preset, en
  and and_3 (and_3_out, d_ff_1_q, step);
  and and_4 (and_4_out, clock, d_ff_2_q);
  or or_1 (C, and_3_out, and_4_out);
endmodule
